# Fritzing sketch full_schematic (saved by Fritzing 0.9.3b)
breadboards: 2

parts:
  Aduino_Uno = Arduino Uno (Rev3)
  U1 = MCP4725 [package=SOT23-6]
  Q1 = NPN-Transistor [package="TO92 [THT]"]
  J1 = Piezo Speaker
  LED2 = LED - 5mm [color="Green (555nm)" package="5 mm [THT]"]
  LED1 = RGB LED (com. cathode, rbg) [package="5 mm [THT]"]
  BioRay_Laser = mystery part, 1 pin [chip_label=?]
  R1 = Resistor [tolerance=±5% resistance=2.2k package=THT]
  Manta_Camera = mystery part, 4 pins [chip_label=?]
  R2 = Resistor [tolerance=±5% resistance=2.2k package=THT]
  Raspberry_Pi_3_B+ = Raspberry Pi 3 [part_number=RPI-3-V1.2]  # not connected
  U3 = 74*32 [package=sot353]
  Safety_Interlock = mystery part, 1 pin [chip_label=ILOCK]
  R3 = Resistor [tolerance=±5% resistance=2.2k package=THT]
  Interlock_override = Tilt Switch [package=THT]
  R4 = Resistor [tolerance=±5% resistance=2.2k package=THT]

nets:
  N1: Aduino_Uno.A2, U3.A, Safety_Interlock.pin1, R3.Pin_1
  N2: Aduino_Uno.A3, U3.B, Interlock_override.Pin_2, R4.Pin_1
  N3: Aduino_Uno.A4/SDA, U1.SDA
  N4: Aduino_Uno.A5/SCL, U1.SCL
  N5: Aduino_Uno.D9_PWM, LED1.green_anode
  N6: Aduino_Uno.D10_PWM/SS, LED1.blue_anode
  N7: Aduino_Uno.D11_PWM/MOSI, LED1.red_anode
  N8: Aduino_Uno.D2, R1.Pin_1, Manta_Camera.pin3
  N9: Aduino_Uno.D3_PWM, Manta_Camera.pin1
  N10: Aduino_Uno.D5_PWM, LED2.anode
  N11: Aduino_Uno.D6_PWM, J1.pin2
  N12: Aduino_Uno.RESET, Q1.E
  5V: Aduino_Uno.5V, Manta_Camera.pin4, U3.VCC
  GND: Aduino_Uno.GND, U1.VSS, Q1.C, J1.pin1, LED2.cathode, LED1.common_cathode, R1.Pin_0, Manta_Camera.pin2, U3.GND, R3.Pin_0, Interlock_override.Pin_1, R4.Pin_0
  N13: U1.VDD, U3.Y
  N14: U1.VOUT, BioRay_Laser.pin1
  N15: Q1.B, R2.Pin_0
